# Fritzing sketch Fritzing Diagram (saved by Fritzing 0.9.3b)
breadboards: 3

parts:
  Part1 = Adafruit Metro Without Headers [part_number="Adafruit #2466"]
  Part2 = Soil Moisture Sensor
  Part3 = Soil Moisture Sensor
  Part4 = Soil Moisture Sensor
  Part5 = Soil Moisture Sensor
  R1 = Photocell (LDR) [package=THT]
  Part6 = KY-019 5V Relay Module [package="Breakout board"]
  Part7 = KY-019 5V Relay Module [package="Breakout board"]
  Part8 = KY-019 5V Relay Module [package="Breakout board"]
  Part9 = KY-019 5V Relay Module [package="Breakout board"]
  S1 = Pushbutton [package="[THT]"]
  R2 = Rotary Potentiometer (Large) [maximum_resistance=100kΩ package=THT]
  M1 = DC Motor
  M2 = DC Motor
  M3 = DC Motor
  M4 = DC Motor
  R3 = Resistor [tolerance=±5% resistance=220 package=THT]
  Water_Level_Sensor1 = Water Level Sensor
  Part10 = KY-019 5V Relay Module [package="Breakout board"]
  LCD1 = LCD screen
  LED1 = LED - 5mm [color="Red (633nm)" package="5 mm [THT]"]
  R4 = Resistor [tolerance=±5% resistance=220 package=THT]

nets:
  N1: Part1.AD0, Water_Level_Sensor1.SIG
  N2: Part1.AD1, R1.pin_1, R3.Pin_0
  N3: Part1.AD2, Part2.SIG
  N4: Part1.AD3, Part3.SIG
  N5: Part1.AD4/SDA, Part4.SIG
  N6: Part1.AD5/SCL, Part5.SIG
  N7: Part1.SCK, LCD1.DB7
  N8: Part1.MISO, LCD1.DB6
  N9: Part1.MOSI, LCD1.DB5
  N10: Part1.SS, LCD1.DB4
  N11: Part1.IO9, LCD1.E
  N12: Part1.IO8, LCD1.RS
  N13: Part1.IO7, S1.Pin_1, S1.Pin_2, R4.Pin_0
  N14: Part1.IO6, Part10.S
  N15: Part1.IO5, Part9.S
  N16: Part1.IO4, Part7.S
  N17: Part1.IO3, Part6.S
  N18: Part1.IO2, Part8.S
  VCC: Part1.3.3V, Part2.VCC, Part3.VCC, Part4.VCC, Part5.VCC, R1.pin_0, Water_Level_Sensor1.VCC
  +5V: Part1.+5V, Part6.+, Part7.+, Part8.+, Part9.+, S1.Pin_3, S1.Pin_4, R2.leg2, Part10.+, LCD1.VDD, LCD1.LED+
  GND: Part1.GND, Part2.GND, Part3.GND, Part4.GND, Part5.GND, Part6.-, Part7.-, Part8.-, Part9.-, R2.leg1, R3.Pin_1, Water_Level_Sensor1.GND, Part10.-, LCD1.VSS, LCD1.LED-, R4.Pin_1
  N19: Part6.Common, M2.pin_1
  N20: Part6.NO, M2.pin_2
  N21: Part7.Common, M4.pin_1
  N22: Part7.NO, M4.pin_2
  N23: Part8.Common, M3.pin_1
  N24: Part8.NO, M3.pin_2
  N25: Part9.Common, M1.pin_1
  N26: Part9.NO, M1.pin_2
  N27: R2.wiper, LCD1.V0
  N28: Part10.Common, LED1.cathode
  N29: Part10.NO, LED1.anode

custom parts:
  Adafruit Metro Without Headers: We sure love the ATmega328 here at Adafruit, and we use them a lot for our own projects. The processor has plenty of GPIO, Analog inputs, hardware UART SPI and I2C, timers and PWM galore - just enough for most simple projects. When we need to go small, we use a Pro Trinket 3V or 5V, but when size isn't as much of a concern, and a USB-serial converter is required, we reach for an Adafruit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
  KY-019 5V Relay Module: KY-019 5V Relay module, used to control AC circuits.
  Water Level Sensor: A water level sensor. This sensor operates at 3V to 5V. The Sig (signal) pin outputs an analogue signal that is in proportion to the amount of water in contact with the sensor.
